// Logisim project Final_Project.circ as structural Verilog: 7 circuits, main circuit ALU
module ALU (
  input  [11:0] InputA,
  input  [2:0] ALUOP,
  input  [11:0] InputB,
  output V,
  output N,
  output C,
  output Z,
  output [11:0] R
);

  wire not_2_out, xnor_1_out, xor_1_out;
  wire [11:0] and_1_out, cla_12_bit_1_output_s, not_1_out, or_1_out, shifter_1_out, shifter_2_out,
       shifter_3_out;

  DipSwitch #(.number(12)) Input_A (
    .sw1(InputA[0]), .sw2(InputA[1]), .sw3(InputA[2]), .sw4(InputA[3]), .sw5(InputA[4]), .sw6(InputA[5]),
    .sw7(InputA[6]), .sw8(InputA[7]), .sw9(InputA[8]), .sw10(InputA[9]), .sw11(InputA[10]), .sw12(InputA[11]));
  DipSwitch #(.number(12)) Input_B (
    .sw1(InputB[0]), .sw2(InputB[1]), .sw3(InputB[2]), .sw4(InputB[3]), .sw5(InputB[4]), .sw6(InputB[5]),
    .sw7(InputB[6]), .sw8(InputB[7]), .sw9(InputB[8]), .sw10(InputB[9]), .sw11(InputB[10]), .sw12(InputB[11]));
  Shifter #(.width(12)) shifter_1 (.in(InputA), .\dist (4'b0001), .out(shifter_1_out));
  Shifter #(.shift("lr"), .width(12)) shifter_2 (.in(InputA), .\dist (4'b0001), .out(shifter_2_out));
  Shifter #(.shift("ar"), .width(12)) shifter_3 (.in(InputA), .\dist (4'b0001), .out(shifter_3_out));
  assign not_1_out = ~InputA;  // NOT_Gate not_1, 12 bits wide
  assign and_1_out = InputA & InputB;  // AND_Gate and_1, 12 bits wide
  assign or_1_out = InputA | InputB;  // OR_Gate or_1, 12 bits wide
  CLA_12_bit cla_12_bit_1 (
    .Input_B(InputB), .Input_A(InputA), .Mode(ALUOP[0]), .Carry_out(C), .Output_S(cla_12_bit_1_output_s));
  // DipSwitch #(.number(3)) Opcode: pin names not known; wires that end beside it: ALUOP[0], ALUOP[1], ALUOP[2]
  Multiplexer #(.select(3), .width(12)) multiplexer_1 (
    .in0(cla_12_bit_1_output_s), .in1(cla_12_bit_1_output_s), .in2(and_1_out), .in3(or_1_out),
    .in4(not_1_out), .in5(shifter_1_out), .in6(shifter_2_out), .in7(shifter_3_out), .out({N, R[10:0]}),
    .sel(ALUOP));
  not not_2 (not_2_out, ALUOP[1]);
  LED Carry_flag (.in(C));
  DipSwitch #(.number(12)) Write_Data (
    .sw1(R[0]), .sw2(R[1]), .sw3(R[2]), .sw4(R[3]), .sw5(R[4]), .sw6(R[5]), .sw7(R[6]), .sw8(R[7]),
    .sw9(R[8]), .sw10(R[9]), .sw11(R[10]), .sw12(N));
  NotExactlyOne xnor_1 (.out(xnor_1_out), .in0(InputA[11]), .in1(ALUOP[0]), .in2(InputB[11]));
  xor xor_1 (xor_1_out, InputA[11], N);
  and and_2 (V, xnor_1_out, xor_1_out, not_2_out);
  LED Overflow (.in(V));
  nor nor_1 (Z, R[0], R[1], R[2], R[3], R[4], R[5], R[6], R[7], R[8], R[9], R[10], N);
  LED Negative_flag (.in(N));
  LED Zero_flag (.in(Z));

  assign R[11] = N;
endmodule

module CLA_12_bit (
  input  [11:0] Input_B,
  input  [11:0] Input_A,
  input  Mode,
  output Carry_out,
  output [11:0] Output_S
);

  wire four_bit_cla_2_carryout, four_bit_cla_3_carryout;
  wire [3:0] bit_extender_1_out, xor_1_out, xor_2_out, xor_3_out;

  assign xor_1_out = Input_B[11:8] ^ bit_extender_1_out;  // XOR_Gate xor_1, 4 bits wide
  Four_bit_CLA four_bit_cla_1 (
    .InputA(Input_A[11:8]), .M_CarryIn(four_bit_cla_2_carryout), .InputB(xor_1_out),
    .OutputS(Output_S[11:8]), .CarryOut(Carry_out));
  assign xor_2_out = Input_B[7:4] ^ bit_extender_1_out;  // XOR_Gate xor_2, 4 bits wide
  Four_bit_CLA four_bit_cla_2 (
    .InputA(Input_A[7:4]), .M_CarryIn(four_bit_cla_3_carryout), .InputB(xor_2_out), .OutputS(Output_S[7:4]),
    .CarryOut(four_bit_cla_2_carryout));
  assign xor_3_out = Input_B[3:0] ^ bit_extender_1_out;  // XOR_Gate xor_3, 4 bits wide
  Four_bit_CLA four_bit_cla_3 (
    .InputA(Input_A[3:0]), .M_CarryIn(Mode), .InputB(xor_3_out), .OutputS(Output_S[3:0]),
    .CarryOut(four_bit_cla_3_carryout));
  assign bit_extender_1_out = {{3{Mode}}, Mode};  // Bit_Extender bit_extender_1
endmodule

module Four_bit_CLA (
  input  [3:0] InputA,
  input  M_CarryIn,
  input  [3:0] InputB,
  output [3:0] OutputS,
  output CarryOut
);

  wire and_1_out, and_2_out, and_3_out, and_4_out, and_5_out, and_6_out, and_7_out, and_8_out, or_1_out,
       or_2_out, or_3_out, xor_1_out, xor_2_out, xor_3_out, xor_4_out;

  xor xor_1 (xor_1_out, InputA[0], InputB[0]);
  xor xor_2 (xor_2_out, InputA[1], InputB[1]);
  xor xor_3 (xor_3_out, InputA[2], InputB[2]);
  xor xor_4 (xor_4_out, InputA[3], InputB[3]);
  xor xor_5 (OutputS[0], M_CarryIn, xor_1_out);
  and and_1 (and_1_out, xor_1_out, M_CarryIn);
  and and_2 (and_2_out, InputA[0], InputB[0]);
  xor xor_6 (OutputS[1], or_1_out, xor_2_out);
  and and_3 (and_3_out, or_1_out, xor_2_out);
  and and_4 (and_4_out, InputA[1], InputB[1]);
  xor xor_7 (OutputS[2], or_2_out, xor_3_out);
  and and_5 (and_5_out, or_2_out, xor_3_out);
  and and_6 (and_6_out, InputA[2], InputB[2]);
  xor xor_8 (OutputS[3], or_3_out, xor_4_out);
  and and_7 (and_7_out, or_3_out, xor_4_out);
  and and_8 (and_8_out, InputA[3], InputB[3]);
  or or_1 (or_1_out, and_1_out, and_2_out);
  or or_2 (or_2_out, and_3_out, and_4_out);
  or or_3 (or_3_out, and_5_out, and_6_out);
  or or_4 (CarryOut, and_7_out, and_8_out);
  LED Cout (.in(CarryOut));
endmodule

module Register_File (
  input  [2:0] RA1,
  input  [2:0] RA2,
  input  [2:0] WA3,
  input  [11:0] WD3,
  input  Write_Enable,
  output [11:0] OR0,
  output [11:0] RD1,
  output [11:0] RD2
);

  wire and_1_out, and_2_out, and_3_out, and_4_out, and_5_out, and_6_out, and_7_out, and_8_out, CLK_out,
       decoder_1_out0, decoder_1_out1, decoder_1_out2, decoder_1_out3, decoder_1_out4, decoder_1_out5,
       decoder_1_out6, decoder_1_out7;
  wire [11:0] register_2_q, register_3_q, register_4_q, register_5_q, register_6_q, register_7_q,
       register_8_q;

  DipSwitch #(.number(3)) Read_Register_1_R1 (.sw1(RA1[0]), .sw2(RA1[1]), .sw3(RA1[2]));
  DipSwitch #(.number(3)) Read_Register_2_R2 (.sw1(RA2[0]), .sw2(RA2[1]), .sw3(RA2[2]));
  DipSwitch #(.number(3)) Write_Register_W (.sw1(WA3[0]), .sw2(WA3[1]), .sw3(WA3[2]));
  DipSwitch #(.number(12)) Write_Data (
    .sw1(WD3[0]), .sw2(WD3[1]), .sw3(WD3[2]), .sw4(WD3[3]), .sw5(WD3[4]), .sw6(WD3[5]), .sw7(WD3[6]),
    .sw8(WD3[7]), .sw9(WD3[8]), .sw10(WD3[9]), .sw11(WD3[10]), .sw12(WD3[11]));
  Decoder #(.select(3)) decoder_1 (
    .out0(decoder_1_out0), .out1(decoder_1_out1), .out2(decoder_1_out2), .out3(decoder_1_out3),
    .out4(decoder_1_out4), .out5(decoder_1_out5), .out6(decoder_1_out6), .out7(decoder_1_out7), .sel(WA3));  // open: en
  and and_1 (and_1_out, decoder_1_out0, Write_Enable);
  and and_2 (and_2_out, decoder_1_out1, Write_Enable);
  and and_3 (and_3_out, decoder_1_out2, Write_Enable);
  and and_4 (and_4_out, decoder_1_out3, Write_Enable);
  and and_5 (and_5_out, decoder_1_out4, Write_Enable);
  and and_6 (and_6_out, decoder_1_out5, Write_Enable);
  and and_7 (and_7_out, decoder_1_out6, Write_Enable);
  and and_8 (and_8_out, decoder_1_out7, Write_Enable);
  Clock CLK (.out(CLK_out));
  Register #(.width(12)) register_1 (.D(WD3), .en(Write_Enable), .clk(CLK_out), .Q(OR0), .clr(and_1_out));
  Register #(.width(12)) register_2 (.D(WD3), .en(Write_Enable), .clk(CLK_out), .Q(register_2_q), .clr(and_2_out));
  Register #(.width(12)) register_3 (.D(WD3), .en(Write_Enable), .clk(CLK_out), .Q(register_3_q), .clr(and_3_out));
  Register #(.width(12)) register_4 (.D(WD3), .en(Write_Enable), .clk(CLK_out), .Q(register_4_q), .clr(and_4_out));
  Register #(.width(12)) register_5 (.D(WD3), .en(Write_Enable), .clk(CLK_out), .Q(register_5_q), .clr(and_5_out));
  Register #(.width(12)) register_6 (.D(WD3), .en(Write_Enable), .clk(CLK_out), .Q(register_6_q), .clr(and_6_out));
  Register #(.width(12)) register_7 (.D(WD3), .en(Write_Enable), .clk(CLK_out), .Q(register_7_q), .clr(and_7_out));
  Register #(.width(12)) register_8 (.D(WD3), .en(Write_Enable), .clk(CLK_out), .Q(register_8_q), .clr(and_8_out));
  Multiplexer #(.disabled("Z"), .select(3), .width(12)) multiplexer_1 (
    .in0(OR0), .in1(register_2_q), .in2(register_3_q), .in3(register_4_q), .in4(register_5_q),
    .in5(register_6_q), .in6(register_7_q), .in7(register_8_q), .out(RD2), .sel(RA2));
  Multiplexer #(.disabled("Z"), .select(3), .width(12)) multiplexer_2 (
    .in0(OR0), .in1(register_2_q), .in2(register_3_q), .in3(register_4_q), .in4(register_5_q),
    .in5(register_6_q), .in6(register_7_q), .in7(register_8_q), .out(RD1), .sel(RA1));
  DipSwitch #(.number(12)) Read_Data_1 (
    .sw1(RD1[0]), .sw2(RD1[1]), .sw3(RD1[2]), .sw4(RD1[3]), .sw5(RD1[4]), .sw6(RD1[5]), .sw7(RD1[6]),
    .sw8(RD1[7]), .sw9(RD1[8]), .sw10(RD1[9]), .sw11(RD1[10]), .sw12(RD1[11]));
  DipSwitch #(.number(12)) Read_Data_2 (
    .sw1(RD2[0]), .sw2(RD2[1]), .sw3(RD2[2]), .sw4(RD2[3]), .sw5(RD2[4]), .sw6(RD2[5]), .sw7(RD2[6]),
    .sw8(RD2[7]), .sw9(RD2[8]), .sw10(RD2[9]), .sw11(RD2[10]), .sw12(RD2[11]));
endmodule

module FLAGS_Register (
  input  N,
  input  Z,
  input  C,
  input  V,
  input  NZW,
  input  Reset,
  input  CVW,
  input  FlagsW,
  input  [11:0] D12,
  output Nq,
  output Zq,
  output Cq,
  output Vq,
  output [11:0] Q12
);

  wire CLK_out, or_1_out, or_2_out;
  wire [1:0] multiplexer_1_out, multiplexer_2_out;

  or or_1 (or_1_out, NZW, FlagsW);
  or or_2 (or_2_out, FlagsW, CVW);
  DipSwitch #(.number(12)) D_12 (
    .sw1(D12[0]), .sw2(D12[1]), .sw3(D12[2]), .sw4(D12[3]), .sw5(D12[4]), .sw6(D12[5]), .sw7(D12[6]),
    .sw8(D12[7]), .sw9(D12[8]), .sw10(D12[9]), .sw11(D12[10]), .sw12(D12[11]));
  DipSwitch #(.number(2)) dipswitch_1 (.sw1(N), .sw2(Z));
  DipSwitch #(.number(2)) dipswitch_2 (.sw1(C), .sw2(V));
  Clock CLK (.out(CLK_out));
  Multiplexer #(.disabled("Z"), .width(2)) multiplexer_1 (
    .in0(D12[1:0]), .in1({Z, N}), .out(multiplexer_1_out), .sel(FlagsW));
  Multiplexer #(.disabled("Z"), .width(2)) multiplexer_2 (
    .in0(D12[3:2]), .in1({V, C}), .out(multiplexer_2_out), .sel(FlagsW));
  Register #(.width(2)) register_1 (.D(multiplexer_1_out), .en(or_1_out), .clk(CLK_out), .Q({Zq, Nq}), .clr(Reset));
  Register #(.width(2)) register_2 (.D(multiplexer_2_out), .en(or_2_out), .clk(CLK_out), .Q({Vq, Cq}), .clr(Reset));

  assign Q12 = D12;
endmodule

module Controller (
  input  [11:0] IWord,
  output MOVC,
  output MOVF,
  output RegW,
  output FlagsW,
  output NZW,
  output CVW,
  output B,
  output [2:0] ALUOP
);

  wire and_2_out, and_3_out, and_4_out, and_5_out, decoder_1_out0, decoder_1_out1, decoder_1_out2,
       decoder_1_out3, decoder_1_out4, decoder_2_out0, decoder_2_out1, decoder_2_out2, decoder_2_out3,
       decoder_2_out4, decoder_2_out5, undriven;

  // DipSwitch #(.number(12)) Instruction_word: pin names not known; wires that end beside it: IWord[0], IWord[1], IWord[2], IWord[3], IWord[4], IWord[5], IWord[6], IWord[7], IWord[8], IWord[9], IWord[10], IWord[11]
  Decoder #(.select(3)) decoder_1 (
    .out0(decoder_1_out0), .out1(decoder_1_out1), .out2(decoder_1_out2), .out3(decoder_1_out3),
    .out4(decoder_1_out4), .out6(MOVC), .out7(B), .sel(IWord[2:0]));  // open: out5, en
  Decoder #(.select(3)) decoder_2 (
    .out0(decoder_2_out0), .out1(decoder_2_out1), .out2(decoder_2_out2), .out3(decoder_2_out3),
    .out4(decoder_2_out4), .out5(decoder_2_out5), .sel(IWord[5:3]));  // open: out6, out7, en
  and and_1 (MOVF, decoder_1_out4, decoder_2_out5);
  and and_2 (and_2_out, decoder_1_out4, decoder_2_out0);
  and and_3 (and_3_out, decoder_1_out4, decoder_2_out1);
  and and_4 (and_4_out, decoder_1_out4, decoder_2_out2);
  and and_5 (and_5_out, decoder_1_out4, decoder_2_out3);
  and and_6 (FlagsW, decoder_1_out4, decoder_2_out4);
  or or_1 (CVW, decoder_1_out0, decoder_1_out1);
  or or_2 (RegW, MOVF, MOVC, decoder_1_out0, decoder_1_out1, decoder_1_out2, decoder_1_out3, and_2_out, and_3_out, and_4_out, and_5_out);
  or or_3 (NZW, decoder_1_out0, decoder_1_out1, decoder_1_out2, decoder_1_out3, and_2_out, and_3_out, and_4_out, and_5_out);
  Priority_Encoder priority_encoder_1 (
    .in0(decoder_1_out0), .in1(decoder_1_out1), .in2(decoder_1_out2), .in3(decoder_1_out3), .in4(and_2_out),
    .in5(and_3_out), .in6(and_4_out), .in7(and_5_out), .out(ALUOP), .en_in(undriven));  // open: gs, en_out

  // Other names for the same wires on the sheet: Op[2:0] = IWord[2:0]; Rm[2:0] = IWord[5:3]
endmodule

module NISC_CPU (
  input  Branch_taken,
  input  Instruction_fetch_en,
  input  CLK,
  input  RESET,
  input  Reset_Flags,
  output [11:0] out_6,
  output [11:0] Instruction
);

  wire alu_1_c, alu_1_n, alu_1_v, alu_1_z, clock_1_out, controller_1_cvw, controller_1_flagsw,
       controller_1_movc, controller_1_nzw, controller_1_regw, flags_register_1_cq, flags_register_1_nq,
       flags_register_1_vq, flags_register_1_zq;
  wire [2:0] controller_1_aluop;
  wire [11:0] adder_1_out, adder_2_out, alu_1_r, bit_extender_1_out, bit_extender_2_out, multiplexer_1_out,
       multiplexer_2_out, multiplexer_3_out, register_file_1_or0, register_file_1_rd1;

  assign bit_extender_1_out = {{6{Instruction[8]}}, Instruction[8:3]};  // Bit_Extender bit_extender_1
  Clock clock_1 (.out(clock_1_out));
  Adder #(.width(12)) adder_1 (.a(out_6), .b(12'h1), .out(adder_1_out));  // open: cin, cout
  Adder #(.width(12)) adder_2 (.a(out_6), .b(bit_extender_1_out), .out(adder_2_out));  // open: cin, cout
  Multiplexer #(.width(12)) multiplexer_1 (
    .in0(adder_1_out), .in1(adder_2_out), .out(multiplexer_1_out), .sel(Branch_taken));
  Register #(.width(12)) register_1 (.D(multiplexer_2_out), .clk(clock_1_out), .Q(out_6), .clr(RESET));  // open: en
  Multiplexer #(.width(12)) multiplexer_2 (
    .in0(out_6), .in1(multiplexer_1_out), .out(multiplexer_2_out), .sel(Instruction_fetch_en));
  ROM #(.addrWidth(12), .dataWidth(12)) rom_1 (.addr(out_6), .data(Instruction));
  assign bit_extender_2_out = {{6{Instruction[8]}}, Instruction[8:3]};  // Bit_Extender bit_extender_2
  Controller controller_1 (
    .IWord(Instruction), .MOVC(controller_1_movc), .RegW(controller_1_regw), .FlagsW(controller_1_flagsw),
    .NZW(controller_1_nzw), .CVW(controller_1_cvw), .ALUOP(controller_1_aluop));  // open: MOVF, B
  Multiplexer #(.width(12)) multiplexer_3 (
    .in0(register_file_1_rd1), .in1(bit_extender_2_out), .out(multiplexer_3_out), .sel(controller_1_movc));
  ALU alu_1 (
    .InputA(register_file_1_or0), .ALUOP(controller_1_aluop), .InputB(multiplexer_3_out), .V(alu_1_v),
    .N(alu_1_n), .C(alu_1_c), .Z(alu_1_z), .R(alu_1_r));
  Register_File register_file_1 (
    .RA1(Instruction[5:3]), .RA2(Instruction[8:6]), .WA3(Instruction[11:9]), .WD3(alu_1_r),
    .Write_Enable(controller_1_regw), .OR0(register_file_1_or0), .RD1(register_file_1_rd1));  // open: RD2
  LED led_1 (.in(flags_register_1_nq));
  FLAGS_Register flags_register_1 (
    .N(alu_1_n), .Z(alu_1_z), .C(alu_1_c), .V(alu_1_v), .NZW(controller_1_nzw), .Reset(Reset_Flags),
    .CVW(controller_1_cvw), .FlagsW(controller_1_flagsw), .Nq(flags_register_1_nq), .Zq(flags_register_1_zq),
    .Cq(flags_register_1_cq), .Vq(flags_register_1_vq));  // open: D12, Q12
  LED led_2 (.in(flags_register_1_zq));
  LED led_3 (.in(flags_register_1_cq));
  LED led_4 (.in(flags_register_1_vq));

  // Other names for the same wires on the sheet: Imm[5:0] = Instruction[8:3]; Rm[2:0] = Instruction[5:3];
  //   Rn[2:0] = Instruction[8:6]; Op[2:0] = Instruction[2:0]; Rd[2:0] = Instruction[11:9]

  // Notes on the sheet:
  //   contents of rom_1 (hex, n*v repeats v):
  //   3c3 f78 6d6 c20 766 572 736 96f 6e3 d22 312 e30 222 65 6e6 36f 646 96e 673 d22 555 446 2d3 822 207
  //   374 616 e64 616 c6f 6e6 53d 226 e6f 223 f3e d0 a3c 707 26f 6a6 563 742 73 6f7 572 636 53d 223 32e
  //   392 e30 222 76 657 273 696 f6e 3d2 231 2e3 22 3e0 d0a 202 54 686 973 206 669 6c6 520 697 320 696 e74
  //   656 e64 656 420 746 f20 626 520 6c6 f61 646 564 206 279 204 c6f 676 973 696 d2d 657 66f 6c7 574 696
  //   f6e 207 633 2e3 92e 302 868 747 470 733 a2f 2f6 769 746 875 622 e63 6f6 d2f 6c6 f67 697 369 6d2 d65
  //   766 f6c 757 469 6f6 e2f 292 e0d a0 d0a 202 3c 6c6 962 206 465 736 33d 222 357 697 269 6e6 722 206
  //   e61 6d6 53d 223 22 3e0 d0a 202 20 203 c74 6f6 f6c 206 e61 6d6 53d 225 69 6e2 23e d0 a20 202 20 202
  //   3c 612 6e 616 d65 3d2 261 707 65 617 261 6e6 365 222 76 616 c3d 226 36c 617 373 696 322 2f3 e0d a2
  //   20 202 3c 2f7 46f 6f6 c3e d0 a20 203 c2f 6c6 962 3e0 d0a 202 3c 6c6 962 206 465 736 33d 222 347 617
  //   465 732 220 6e6 16d 653 d22 312 23e d0 a20 202 20 3c7 46f 6f6 c20 6e6 16d 653 d22 4e4 f52 204 761
  //   746 522 3e0 d0a 202 20 202 20 3c6 120 6e6 16d 653 d22 696 e70 757 473 222 76 616 c3d 223 822 2f3 e0d
  //   a2 20 202 3c 2f7 46f 6f6 c3e d0 a20 203 c2f 6c6 962 3e0 d0a 202 3c 6c6 962 206 465 736 33d 222 350
  //   6c6 578 657 273 222 6e 616 d65 3d2 232 222 f3e d0 a20 203 c6c 696 220 646 573 633 d22 234 172 697
  //   468 6d6 574 696 322 206 e61 6d6 53d 223 322 2f3 e0d a2 20 3c6 c69 622 64 657 363 3d2 223 4d6 56d 6f7
  //   279 222 6e 616 d65 3d2 234 222 f3e d0 a20 203 c6c 696 220 646 573 633 d22 234 92f 4f2 220 6e6 16d
  //   653 d22 352 22f 3e0 d0a 202 3c 6c6 962 206 465 736 33d 222 354 544 c22 206 e61 6d6 53d 223 622 2f3
  //   e0d a2 20 3c6 c69 622 64 657 363 3d2 223 544 34c 222 6e 616 d65 3d2 237 222 f3e d0 a20 203 c6c 696
  //   220 646 573 633 d22 234 261 736 522 206 e61 6d6 53d 223 822 3e0 d0a 202 20 203 c74 6f6 f6c 206 e61
  //   6d6 53d 225 465 787 420 546 f6f 6c2 23e d0 a20 202 20 202 3c 612 6e 616 d65 3d2 274 657 874 222 76
  //   616 c3d 225 265 726 f75 746 520 696 620 796 f75 206 e65 656 420 746 f2e 222 f3e d0 a20 202 20 3c2
  //   f74 6f6 f6c 3e0 d0a 202 3c 2f6 c69 623 e0d a2 20 3c6 c69 622 64 657 363 3d2 223 424 648 2d5 72 616
  //   b74 696 b61 222 6e 616 d65 3d2 239 222 f3e d0 a20 203 c6c 696 220 646 573 633 d22 234 96e 707 574
  //   2f4 f75 747 75 742 d45 787 472 612 220 6e6 16d 653 d22 313 22 2f3 e0d a2 20 3c6 c69 622 64 657 363
  //   3d2 223 536 f63 222 6e 616 d65 3d2 231 312 22f 3e0 d0a 202 3c 6d6 169 6e2 6e 616 d65 3d2 26d 616 96e
  //   222 f3e d0 a20 203 c6f 707 469 6f6 e73 3e0 d0a 202 20 203 c61 206 e61 6d6 53d 226 761 746 555 6e6
  //   465 666 96e 656 422 207 661 6c3 d22 696 76e 6f7 265 222 f3e d0 a20 202 20 3c6 120 6e6 16d 653 d22
  //   736 96d 6c6 96d 697 422 207 661 6c3 d22 313 30 302 22f 3e0 d0a 202 20 203 c61 206 e61 6d6 53d 227
  //   369 6d7 261 6e6 422 207 661 6c3 d22 302 22f 3e0 d0a 202 3c 2f6 f70 746 96f 6e7 33e d0 a20 203 c6d
  //   617 70 696 e67 733 e0d a2 20 202 3c 746 f6f 6c2 6c 696 23d 223 822 206 d61 703 d22 427 574 746 f6e
  //   322 220 6e6 16d 653 d22 506 f6b 652 54 6f6 f6c 222 f3e d0 a20 202 20 3c7 46f 6f6 c20 6c6 962 3d2 238
  //   222 6d 617 3d 224 275 747 46f 6e3 322 206 e61 6d6 53d 224 d65 6e7 520 546 f6f 6c2 22f 3e0 d0a 202 20
  //   203 c74 6f6 f6c 206 c69 623 d22 382 220 6d6 170 3d2 243 747 26c 204 275 747 46f 6e3 122 206 e61 6d6
  //   53d 224 d65 6e7 520 546 f6f 6c2 22f 3e0 d0a 202 3c 2f6 d61 707 69 6e6 773 3e0 d0a 202 3c 746 f6f 6c6
  //   261 723 e0d a2 20 202 3c 746 f6f 6c2 6c 696 23d 223 822 206 e61 6d6 53d 225 6f 6b6 520 546 f6f 6c2
  //   22f 3e0 d0a 202 20 203 c74 6f6 f6c 206 c69 623 d22 382 220 6e6 16d 653 d22 456 469 742 54 6f6 f6c
  //   222 f3e d0 a20 202 20 3c7 46f 6f6 c20 6c6 962 3d2 238 222 6e 616 d65 3d2 257 697 269 6e6 720 546 f6f
  //   6c2 22f 3e0 d0a 202 20 203 c74 6f6 f6c 206 c69 623 d22 382 220 6e6 16d 653 d22 546 578 742 54 6f6
  //   f6c 223 e0d a2 20 202 20 203 c61 206 e61 6d6 53d 227 465 787 422 207 661 6c3 d22 526 572 6f7 574 652
  //   69 662 79 6f7 520 6e6 565 642 74 6f2 e22 2f3 e0d a2 20 202 3c 2f7 46f 6f6 c3e d0 a20 202 20 3c7 365
  //   702 f3e d0 a20 202 20 3c7 46f 6f6 c20 6c6 962 3d2 230 222 6e 616 d65 3d2 250 696 e22 2f3 e0d a2 20
  //   202 3c 746 f6f 6c2 6c 696 23d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
endmodule
